// Logisim project x47.circ as structural Verilog: 6 circuits, main circuit CPU
module CPU (
);

  wire and_1_out, clock_1_out, cu_1_alu_enable_read, cu_1_enable_write_a, cu_1_enable_write_b, cu_1_halt,
       cu_1_noop, cu_1_ram_read_enable, cu_1_ram_write_enable, cu_1_register_read_enable,
       cu_1_register_write_enable, not_1_out;
  wire [3:0] alu_1_flags, cu_1_alu_opcode, cu_1_register_address_out;
  wire [7:0] cu_1_ram_address_out;
  wire [31:0] alu_1_output, cu_1_data_out, multiplexer_1_out, multiplexer_2_out, multiplexer_3_out, or_1_out,
       or_2_out, ram_1_data, ram_2_data;

  ALU alu_1 (
    .In(or_1_out), .Op_Code(cu_1_alu_opcode), .Output(alu_1_output), .Read_Enable(cu_1_alu_enable_read),
    .Enable_Write_A(cu_1_enable_write_a), .Enable_Write_B(cu_1_enable_write_b), .Flags(alu_1_flags));
  Multiplexer #(.width(32)) multiplexer_1 (
    .in0({32{1'b0}}), .in1(alu_1_output), .out(multiplexer_1_out), .sel(cu_1_alu_enable_read));  // open: en
  Clock clock_1 (.out(clock_1_out));
  CU cu_1 (
    .Data_In(or_1_out), .RAM_Read_Enable(cu_1_ram_read_enable), .RAM_Write_Enable(cu_1_ram_write_enable),
    .RAM_Address_Out(cu_1_ram_address_out), .Data_Out(cu_1_data_out), .Clock(and_1_out), .NoOp(cu_1_noop),
    .Register_Address_Out(cu_1_register_address_out), .Register_Read_Enable(cu_1_register_read_enable),
    .Register_Write_Enable(cu_1_register_write_enable), .Enable_Write_A(cu_1_enable_write_a),
    .Enable_Write_B(cu_1_enable_write_b), .ALU_OpCode(cu_1_alu_opcode), .Flags(alu_1_flags),
    .ALU_Enable_Read(cu_1_alu_enable_read), .HALT(cu_1_halt));
  and and_1 (and_1_out, clock_1_out, not_1_out);
  not not_1 (not_1_out, cu_1_halt);
  RAM #(.addrWidth(4), .dataWidth(32), .bus("separate")) ram_1 (
    .addr(cu_1_register_address_out), .din(or_1_out), .data(ram_1_data), .str(cu_1_register_write_enable),
    .clk(and_1_out), .ld(cu_1_register_read_enable));  // open: sel, clr
  LED led_1 (.in(cu_1_halt));
  LED led_2 (.in(cu_1_noop));
  assign or_1_out = cu_1_data_out | multiplexer_3_out | or_2_out;  // OR_Gate or_1, 32 bits wide
  assign or_2_out = multiplexer_1_out | multiplexer_2_out;  // OR_Gate or_2, 32 bits wide
  Multiplexer #(.width(32)) multiplexer_2 (
    .in0({32{1'b0}}), .in1(ram_1_data), .out(multiplexer_2_out), .sel(cu_1_register_read_enable));  // open: en
  Multiplexer #(.width(32)) multiplexer_3 (
    .in0({32{1'b0}}), .in1(ram_2_data), .out(multiplexer_3_out), .sel(cu_1_ram_read_enable));  // open: en
  RAM #(.dataWidth(32), .bus("separate")) ram_2 (
    .addr(cu_1_ram_address_out), .din(or_1_out), .data(ram_2_data), .str(cu_1_ram_write_enable),
    .clk(and_1_out), .ld(cu_1_ram_read_enable));  // open: sel, clr

  // Notes on the sheet:
  //   Load Image Of Programs Here
endmodule

module CU (
  input  Clock,
  input  [3:0] Flags,
  input  [31:0] Data_In,
  output HALT,
  output [7:0] RAM_Address_Out,
  output NoOp,
  output RAM_Read_Enable,
  output RAM_Write_Enable,
  output Enable_Write_A,
  output Enable_Write_B,
  output [3:0] ALU_OpCode,
  output ALU_Enable_Read,
  output [3:0] Register_Address_Out,
  output Register_Read_Enable,
  output [31:0] Data_Out,
  output Register_Write_Enable
);

  wire and_4_out, and_5_out, and_6_out, and_7_out, and_8_out, and_9_out, comparator_1_eq, comparator_2_eq,
       d_ff_1_q, d_ff_1_qn, d_ff_2_q, d_ff_2_qn, demultiplexer_2_out0, demultiplexer_2_out1,
       demultiplexer_3_out1, demultiplexer_3_out2, demultiplexer_3_out3, demultiplexer_3_out4,
       demultiplexer_3_out5, demultiplexer_3_out7, not_1_out, not_2_out, not_3_out, not_4_out, or_1_out,
       or_2_out, or_3_out, or_4_out, or_5_out, or_6_out, or_8_out, or_9_out, or_10_out, or_11_out, or_14_out,
       or_16_out, or_18_out;
  wire [0:0] register_1_q_6;
  wire [2:0] register_1_q_4, register_1_q_7;
  wire [3:0] and_2_out, and_3_out, and_11_out, and_12_out, and_13_out, n1_4b_1_out, n1_4b_2_out, n1_4b_3_out,
       n1_4b_4_out, n1_4b_5_out, or_7_out, register_1_q, register_1_q_2, register_1_q_5, subtractor_1_out;
  wire [4:0] register_1_q_3;
  wire [7:0] adder_1_out, and_10_out, and_15_out, multiplexer_1_out, n1_8b_1_out, n1_8b_2_out,
       Program_Counter_q, register_1_q_8;
  wire [31:0] and_14_out, and_16_out, n1_32b_1_out, n1_32b_2_out, n1_32b_3_out, or_19_out, register_2_q;

  Demultiplexer demultiplexer_1 (
    .out0(Enable_Write_A), .out1(Enable_Write_B), .in(demultiplexer_3_out5), .sel(register_1_q_3[4]));  // open: en
  assign ALU_OpCode = {register_1_q_4, register_1_q_3[4]} & n1_4b_1_out;  // AND_Gate and_1, 4 bits wide
  _1_4b u_1_4b_1 (.Enable(ALU_Enable_Read), .Out(n1_4b_1_out));
  _1_4b u_1_4b_2 (.Enable(demultiplexer_3_out7), .Out(n1_4b_2_out));
  assign and_2_out = n1_4b_2_out & register_1_q_5;  // AND_Gate and_2, 4 bits wide
  Subtractor #(.width(4)) subtractor_1 (.a(and_2_out), .b(Flags), .out(subtractor_1_out));  // open: bin, bout
  assign and_3_out = and_2_out & Flags;  // AND_Gate and_3, 4 bits wide
  and and_4 (and_4_out, demultiplexer_3_out7, comparator_1_eq);
  Comparator #(.width(4), .mode("unsigned")) comparator_1 (
    .a(subtractor_1_out), .b(4'b0000), .eq(comparator_1_eq));  // open: gt, lt
  Comparator #(.width(4), .mode("unsigned")) comparator_2 (
    .a(and_3_out), .b(4'b0000), .eq(comparator_2_eq));  // open: gt, lt
  D_Flip_Flop d_ff_1 (.clk(Clock), .D(d_ff_1_qn), .Q(d_ff_1_q), .Qn(d_ff_1_qn), .en(1'b1));  // open: preset, reset
  D_Flip_Flop d_ff_2 (.clk(d_ff_1_q), .D(d_ff_2_qn), .Q(d_ff_2_q), .Qn(d_ff_2_qn), .en(1'b1));  // open: preset, reset
  Demultiplexer demultiplexer_2 (
    .out0(demultiplexer_2_out0), .out1(demultiplexer_2_out1), .in(demultiplexer_3_out7),
    .sel(register_1_q_6[0]));  // open: en
  and and_5 (and_5_out, demultiplexer_2_out0, and_4_out);
  and and_6 (and_6_out, demultiplexer_2_out1, not_1_out);
  not not_1 (not_1_out, comparator_2_eq);
  or or_1 (or_1_out, ALU_Enable_Read, demultiplexer_3_out5);
  or or_2 (or_2_out, and_5_out, and_6_out);
  not not_2 (not_2_out, d_ff_1_q);
  or or_3 (or_3_out, or_2_out, demultiplexer_3_out1);
  not not_3 (not_3_out, d_ff_1_q);
  and and_7 (and_7_out, not_3_out, or_3_out);
  and and_8 (and_8_out, demultiplexer_3_out4, d_ff_1_q);
  and and_9 (and_9_out, demultiplexer_3_out4, not_2_out);
  not not_4 (not_4_out, d_ff_2_q);
  Demultiplexer #(.select(4)) demultiplexer_3 (
    .out0(NoOp), .out1(demultiplexer_3_out1), .out2(demultiplexer_3_out2), .out3(demultiplexer_3_out3),
    .out4(demultiplexer_3_out4), .out5(demultiplexer_3_out5), .out6(ALU_Enable_Read),
    .out7(demultiplexer_3_out7), .out15(HALT), .in(not_4_out), .sel(register_1_q));  // open: out8, out9, out10, out11, out12, out13, out14, en
  assign and_10_out = {register_1_q_4, register_1_q_3} & n1_8b_1_out;  // AND_Gate and_10, 8 bits wide
  or or_4 (or_4_out, demultiplexer_3_out3, demultiplexer_3_out2);
  _1_8b u_1_8b_1 (.Enable(or_4_out), .Out(n1_8b_1_out));
  _1_4b u_1_4b_3 (.Enable(or_5_out), .Out(n1_4b_3_out));
  or or_5 (or_5_out, and_8_out, or_1_out);
  _1_4b u_1_4b_4 (.Enable(or_6_out), .Out(n1_4b_4_out));
  buf or_6 (or_6_out, and_9_out);  // OR_Gate
  _1_4b u_1_4b_5 (.Enable(or_4_out), .Out(n1_4b_5_out));
  assign and_11_out = register_1_q_3[3:0] & n1_4b_3_out;  // AND_Gate and_11, 4 bits wide
  assign or_7_out = and_11_out | and_12_out;  // OR_Gate or_7, 4 bits wide
  assign and_12_out = {register_1_q_4, register_1_q_3[4]} & n1_4b_4_out;  // AND_Gate and_12, 4 bits wide
  assign and_13_out = register_1_q_5 & n1_4b_5_out;  // AND_Gate and_13, 4 bits wide
  buf or_8 (or_8_out, demultiplexer_3_out2);  // OR_Gate
  or or_9 (or_9_out, and_8_out, demultiplexer_3_out5);
  or or_10 (or_10_out, and_9_out, ALU_Enable_Read);
  buf or_11 (or_11_out, demultiplexer_3_out3);  // OR_Gate
  or or_12 (Register_Read_Enable, or_9_out, demultiplexer_3_out3);
  or or_13 (Register_Write_Enable, or_10_out, demultiplexer_3_out2);
  _1_32b u_1_32b_1 (.Enable(or_14_out), .Out(n1_32b_1_out));
  buf or_14 (or_14_out, d_ff_2_q);  // OR_Gate
  assign and_14_out = n1_32b_1_out & Data_In;  // AND_Gate and_14, 32 bits wide
  Multiplexer #(.width(8)) multiplexer_1 (
    .in0(adder_1_out), .in1({register_1_q_4, register_1_q_3}), .out(multiplexer_1_out), .sel(or_3_out));  // open: en
  assign Register_Address_Out = or_7_out | and_13_out;  // OR_Gate or_15, 4 bits wide
  Register #(.width(32), .trigger("high")) register_1 (
    .D(and_14_out), .en(1'b1),
    .Q({register_1_q_8, register_1_q_7, register_1_q_6[0], register_1_q_5, register_1_q_4, register_1_q_3, register_1_q_2, register_1_q}),
    .clk(d_ff_2_q));  // open: clr
  or or_16 (or_16_out, d_ff_2_q, and_7_out);
  Register Program_Counter (.D(multiplexer_1_out), .en(1'b1), .Q(Program_Counter_q), .clk(or_16_out));  // open: clr
  Adder adder_1 (.a(Program_Counter_q), .b(8'h1), .out(adder_1_out));  // open: cin, cout
  _1_32b u_1_32b_2 (.Enable(demultiplexer_3_out4), .Out(n1_32b_2_out));
  Register #(.width(32)) register_2 (.D(Data_In), .en(1'b1), .Q(register_2_q), .clk(Clock));  // open: clr
  assign RAM_Address_Out = and_10_out | and_15_out;  // OR_Gate or_17, 8 bits wide
  assign and_15_out = Program_Counter_q & n1_8b_2_out;  // AND_Gate and_15, 8 bits wide
  _1_8b u_1_8b_2 (.Enable(d_ff_2_q), .Out(n1_8b_2_out));
  assign and_16_out = n1_32b_2_out & register_2_q;  // AND_Gate and_16, 32 bits wide
  buf or_18 (or_18_out, and_9_out);  // OR_Gate
  assign or_19_out = and_16_out;  // OR_Gate or_19, 32 bits wide OR_Gate
  _1_32b u_1_32b_3 (.Enable(1'b0), .Out(n1_32b_3_out));
  Multiplexer #(.width(32)) multiplexer_2 (
    .in0(n1_32b_3_out), .in1(or_19_out), .out(Data_Out), .sel(or_18_out));  // open: en
  or or_20 (RAM_Read_Enable, or_8_out, d_ff_2_q);
  buf or_21 (RAM_Write_Enable, or_11_out);  // OR_Gate
endmodule

module ALU (
  input  Enable_Write_A,
  input  [31:0] In,
  input  Enable_Write_B,
  input  [3:0] Op_Code,
  input  Read_Enable,
  output [31:0] Output,
  output [3:0] Flags
);

  wire [31:0] A_q, adder_1_out, B_q, multiplexer_1_out, n1_32b_1_out, subtractor_1_out;

  Adder #(.width(32)) adder_1 (.a(A_q), .b(B_q), .out(adder_1_out));  // open: cin, cout
  Subtractor #(.width(32)) subtractor_1 (.a(A_q), .b(B_q), .out(subtractor_1_out));  // open: bin, bout
  Multiplexer #(.select(4), .width(32)) multiplexer_1 (
    .in0(adder_1_out), .in1(subtractor_1_out), .out(multiplexer_1_out), .sel(Op_Code));  // open: in2, in3, in4, in5, in6, in7, in8, in9, in10, in11, in12, in13, in14, in15, en
  _1_32b u_1_32b_1 (.Enable(Read_Enable), .Out(n1_32b_1_out));
  assign Output = multiplexer_1_out & n1_32b_1_out;  // AND_Gate and_1, 32 bits wide
  Register #(.width(32), .trigger("high")) A (.D(In), .en(1'b1), .Q(A_q), .clk(Enable_Write_A));  // open: clr
  Register #(.width(32), .trigger("high")) B (.D(In), .en(1'b1), .Q(B_q), .clk(Enable_Write_B));  // open: clr
  Comparator #(.width(32)) comparator_1 (.a(A_q), .b(B_q), .gt(Flags[1]), .eq(Flags[0]), .lt(Flags[2]));
  Comparator #(.width(32), .mode("unsigned")) comparator_2 (.a(A_q), .b({32{1'b0}}), .eq(Flags[3]));  // open: gt, lt
endmodule

module _1_4b (
  input  Enable,
  output [3:0] Out
);

  Multiplexer #(.width(4)) multiplexer_1 (.in0(4'b0000), .in1(4'b1111), .out(Out), .sel(Enable));  // open: en
endmodule

module _1_8b (
  input  Enable,
  output [7:0] Out
);

  Multiplexer #(.width(8)) multiplexer_1 (.in0({8{1'b0}}), .in1({8{1'b1}}), .out(Out), .sel(Enable));  // open: en
endmodule

module _1_32b (
  input  Enable,
  output [31:0] Out
);

  Multiplexer #(.width(32)) multiplexer_1 (.in0({32{1'b0}}), .in1({32{1'b1}}), .out(Out), .sel(Enable));  // open: en
endmodule
